// Logisim project Lab02.circ as structural Verilog: 2 circuits, main circuit main
module main (
  input  In1A,
  input  In1B,
  input  In1C,
  output Out1
);

  wire and_1_out, and_2_out, and_3_out;

  and and_1 (and_1_out, ~In1A, In1B, ~In1C);  // AND_Gate
  and and_2 (and_2_out, In1A, ~In1B, ~In1C);  // AND_Gate
  or or_1 (Out1, and_1_out, and_2_out, and_3_out);
  and and_3 (and_3_out, In1A, In1B, In1C);
endmodule

module Equation_2 (
  input  In2A,
  input  In2B,
  input  In2C,
  input  In2D,
  output Out2
);

  // AND_Gate and_1 has open pins: in0=In2A, out=open
  // AND_Gate and_2 has open pins: in1=In2B, out=open
  // AND_Gate and_3 has open pins: in1=In2C, in2=In2C, out=open
  // AND_Gate and_4 has open pins: in2=In2D, out=open
  // OR_Gate or_1 is placed but not wired

  // Notes on the sheet:
  //   (A'B'CD')+(A'BCD)+(AB'CD')+(ABCD')
endmodule
